# Fritzing sketch Diagrama_conexiones (saved by Fritzing 0.9.4)

parts:
  U2 = Vibration Motor- ROB-08449 [package=vibe-motor-10mm]
  Q1 = NPN-Transistor [package="TO92 [THT]"]
  R1 = Resistor [tolerance=±5% resistance=220 package="1206 [SMD]"]
  D1 = Diode [package=diode-hv]
  U3 = SWITCH_SPDT [package=kps-1290]
  U5 = LIPO-110mAh [package=lipo-110]
  J2 = Micro JST 2 pin-altbb
  Mod3 = gy-906
  J3 = female pin header, 1 pin [form="♀ (female)"]
  J4 = female pin header, 1 pin [form="♀ (female)"]
  J5 = female pin header, 1 pin [form="♀ (female)"]
  J6 = female pin header, 1 pin [form="♀ (female)"]
  M4 = MakerFocus MAX30102
  A3 = XIAO ESP32C3-tht

nets:
  N1: U2.+, Q1.E, D1.A
  N2: U2.-, D1.C, J5.pin1
  N3: Q1.B, R1.Pin_0
  N4: Q1.C, J3.pin1
  N5: R1.Pin_1, J4.pin1
  N6: U3.O, U5.+
  N7: U3.P, U3.S, J2.2
  N8: U5.-, J2.1
  VIN: Mod3.VIN, M4.VIN, A3.Pin_20
  GND: Mod3.GND, M4.GND, A3.Pin_2, A3.Pin_21
  N9: Mod3.SCL, M4.SCL, A3.Pin_14
  N10: Mod3.SDA, M4.SDA, A3.Pin_13
  N11: J6.pin1, A3.Pin_11

notes:
  Ground
  R1
  2N2222
  M1
  3.3 V
  R1.D2
  1N4007
  MAX30102
  GY-906
  Switch
  JST connector
  (a)
  (b)
  (c)

custom parts:
  Micro JST 2 pin-altbb: Micro JST Header: 1.25mm Pitch Miniature Crimping Connector. Single Row right angle Pin Header (THT)
  gy-906: gy-906 Non-contact PIR I2C interface temperature sensor breakout board.
  MakerFocus MAX30102: Oximeter module using the MAX30102 chip. As usual, if you want the mounting holes in pcb, you need to drag a hole over the pad in silkscreen to actually drill the hole (by default they are not drilled)
  XIAO ESP32C3-tht: Seeed Studio XIAO ESP32C3 adopts new RISC-V architecture, supporting both Wi-Fi and BLE wireless connectivities.
